// Digital circuit 4kRAM_16bit.dig as structural Verilog
module _4kRAM_16bit (
  input  [15:0] IN,
  input  LOAD,
  input  [11:0] SEL,
  output [15:0] OUT
);

  wire demultiplexer_1_out_0, demultiplexer_1_out_1, demultiplexer_1_out_2, demultiplexer_1_out_3,
       demultiplexer_1_out_4, demultiplexer_1_out_5, demultiplexer_1_out_6, demultiplexer_1_out_7;
  wire [15:0] _512ram_16bit_1_p4, _512ram_16bit_2_p4, _512ram_16bit_3_p4, _512ram_16bit_4_p4,
       _512ram_16bit_5_p4, _512ram_16bit_6_p4, _512ram_16bit_7_p4, _512ram_16bit_8_p4;

  Demultiplexer #(.Selector_Bits(3)) demultiplexer_1 (
    .sel(SEL[11:9]), .in(LOAD), .out_0(demultiplexer_1_out_0), .out_1(demultiplexer_1_out_1),
    .out_2(demultiplexer_1_out_2), .out_3(demultiplexer_1_out_3), .out_4(demultiplexer_1_out_4),
    .out_5(demultiplexer_1_out_5), .out_6(demultiplexer_1_out_6), .out_7(demultiplexer_1_out_7));
  // _512RAM_16bit _512ram_16bit_1: pin names not known; wires that end beside it: IN, demultiplexer_1_out_0, SEL[8:0], _512ram_16bit_1_p4
  // _512RAM_16bit _512ram_16bit_2: pin names not known; wires that end beside it: IN, demultiplexer_1_out_1, SEL[8:0], _512ram_16bit_2_p4
  // _512RAM_16bit _512ram_16bit_3: pin names not known; wires that end beside it: IN, demultiplexer_1_out_2, SEL[8:0], _512ram_16bit_3_p4
  // _512RAM_16bit _512ram_16bit_4: pin names not known; wires that end beside it: IN, demultiplexer_1_out_3, SEL[8:0], _512ram_16bit_4_p4
  // _512RAM_16bit _512ram_16bit_5: pin names not known; wires that end beside it: IN, demultiplexer_1_out_4, SEL[8:0], _512ram_16bit_5_p4
  // _512RAM_16bit _512ram_16bit_6: pin names not known; wires that end beside it: IN, demultiplexer_1_out_5, SEL[8:0], _512ram_16bit_6_p4
  // _512RAM_16bit _512ram_16bit_7: pin names not known; wires that end beside it: IN, demultiplexer_1_out_6, SEL[8:0], _512ram_16bit_7_p4
  // _512RAM_16bit _512ram_16bit_8: pin names not known; wires that end beside it: IN, demultiplexer_1_out_7, SEL[8:0], _512ram_16bit_8_p4
  Multiplexer #(.Selector_Bits(3), .Bits(16)) multiplexer_1 (
    .sel(SEL[11:9]), .in_0(_512ram_16bit_1_p4), .in_1(_512ram_16bit_2_p4), .in_2(_512ram_16bit_3_p4),
    .in_3(_512ram_16bit_4_p4), .in_4(_512ram_16bit_5_p4), .in_5(_512ram_16bit_6_p4),
    .in_6(_512ram_16bit_7_p4), .in_7(_512ram_16bit_8_p4), .out(OUT));
endmodule
