// Digital circuit 512RAM_16bit.dig as structural Verilog
module _512RAM_16bit (
  input  [15:0] IN,
  input  LOAD,
  input  [8:0] SEL,
  output [15:0] OUT
);

  wire demultiplexer_1_out_0, demultiplexer_1_out_1, demultiplexer_1_out_2, demultiplexer_1_out_3,
       demultiplexer_1_out_4, demultiplexer_1_out_5, demultiplexer_1_out_6, demultiplexer_1_out_7;
  wire [15:0] _64ram_16bit_1_out, _64ram_16bit_2_out, _64ram_16bit_3_out, _64ram_16bit_4_out,
       _64ram_16bit_5_out, _64ram_16bit_6_out, _64ram_16bit_7_out, _64ram_16bit_8_out;

  Demultiplexer #(.Selector_Bits(3)) demultiplexer_1 (
    .sel(SEL[8:6]), .in(LOAD), .out_0(demultiplexer_1_out_0), .out_1(demultiplexer_1_out_1),
    .out_2(demultiplexer_1_out_2), .out_3(demultiplexer_1_out_3), .out_4(demultiplexer_1_out_4),
    .out_5(demultiplexer_1_out_5), .out_6(demultiplexer_1_out_6), .out_7(demultiplexer_1_out_7));
  _64RAM_16bit _64ram_16bit_1 (.LOAD(demultiplexer_1_out_0), .SEL(SEL[5:0]), .IN(IN), .OUT(_64ram_16bit_1_out));
  _64RAM_16bit _64ram_16bit_2 (.LOAD(demultiplexer_1_out_1), .SEL(SEL[5:0]), .IN(IN), .OUT(_64ram_16bit_2_out));
  _64RAM_16bit _64ram_16bit_3 (.LOAD(demultiplexer_1_out_2), .SEL(SEL[5:0]), .IN(IN), .OUT(_64ram_16bit_3_out));
  _64RAM_16bit _64ram_16bit_4 (.LOAD(demultiplexer_1_out_3), .SEL(SEL[5:0]), .IN(IN), .OUT(_64ram_16bit_4_out));
  _64RAM_16bit _64ram_16bit_5 (.LOAD(demultiplexer_1_out_4), .SEL(SEL[5:0]), .IN(IN), .OUT(_64ram_16bit_5_out));
  _64RAM_16bit _64ram_16bit_6 (.LOAD(demultiplexer_1_out_5), .SEL(SEL[5:0]), .IN(IN), .OUT(_64ram_16bit_6_out));
  _64RAM_16bit _64ram_16bit_7 (.LOAD(demultiplexer_1_out_6), .SEL(SEL[5:0]), .IN(IN), .OUT(_64ram_16bit_7_out));
  _64RAM_16bit _64ram_16bit_8 (.LOAD(demultiplexer_1_out_7), .SEL(SEL[5:0]), .IN(IN), .OUT(_64ram_16bit_8_out));
  Multiplexer #(.Selector_Bits(3), .Bits(16)) multiplexer_1 (
    .sel(SEL[8:6]), .in_0(_64ram_16bit_1_out), .in_1(_64ram_16bit_2_out), .in_2(_64ram_16bit_3_out),
    .in_3(_64ram_16bit_4_out), .in_4(_64ram_16bit_5_out), .in_5(_64ram_16bit_6_out),
    .in_6(_64ram_16bit_7_out), .in_7(_64ram_16bit_8_out), .out(OUT));
endmodule
