// Digital circuit 64RAM_16bit.dig as structural Verilog
module _64RAM_16bit (
  input  [15:0] IN,
  input  LOAD,
  input  [5:0] SEL,
  output [15:0] OUT
);

  wire demultiplexer_1_out_0, demultiplexer_1_out_1, demultiplexer_1_out_2, demultiplexer_1_out_3,
       demultiplexer_1_out_4, demultiplexer_1_out_5, demultiplexer_1_out_6, demultiplexer_1_out_7;
  wire [15:0] _8ram_16bit_2_p1, _8ram_16bit_3_p1, _8ram_16bit_4_p1, _8ram_16bit_5_p1, _8ram_16bit_6_p1,
       _8ram_16bit_7_p1, _8ram_16bit_8_p1, undriven;

  Demultiplexer #(.Selector_Bits(3)) demultiplexer_1 (
    .sel(SEL[5:3]), .in(LOAD), .out_0(demultiplexer_1_out_0), .out_1(demultiplexer_1_out_1),
    .out_2(demultiplexer_1_out_2), .out_3(demultiplexer_1_out_3), .out_4(demultiplexer_1_out_4),
    .out_5(demultiplexer_1_out_5), .out_6(demultiplexer_1_out_6), .out_7(demultiplexer_1_out_7));
  // _8RAM_16bit _8ram_16bit_1: pin names not known; wires that end beside it: IN, demultiplexer_1_out_0, SEL[2:0]
  // _8RAM_16bit _8ram_16bit_2: pin names not known; wires that end beside it: _8ram_16bit_2_p1, IN, demultiplexer_1_out_1, SEL[2:0]
  // _8RAM_16bit _8ram_16bit_3: pin names not known; wires that end beside it: _8ram_16bit_3_p1, IN, demultiplexer_1_out_2, SEL[2:0]
  // _8RAM_16bit _8ram_16bit_4: pin names not known; wires that end beside it: _8ram_16bit_4_p1, IN, demultiplexer_1_out_3, SEL[2:0]
  // _8RAM_16bit _8ram_16bit_5: pin names not known; wires that end beside it: _8ram_16bit_5_p1, IN, demultiplexer_1_out_4, SEL[2:0]
  // _8RAM_16bit _8ram_16bit_6: pin names not known; wires that end beside it: _8ram_16bit_6_p1, IN, demultiplexer_1_out_5, SEL[2:0]
  // _8RAM_16bit _8ram_16bit_7: pin names not known; wires that end beside it: _8ram_16bit_7_p1, IN, demultiplexer_1_out_6, SEL[2:0]
  // _8RAM_16bit _8ram_16bit_8: pin names not known; wires that end beside it: _8ram_16bit_8_p1, IN, demultiplexer_1_out_7, SEL[2:0]
  Multiplexer #(.Selector_Bits(3), .Bits(16)) multiplexer_1 (
    .sel(SEL[5:3]), .in_0(_8ram_16bit_2_p1), .in_1(_8ram_16bit_3_p1), .in_2(_8ram_16bit_4_p1),
    .in_3(_8ram_16bit_5_p1), .in_4(_8ram_16bit_6_p1), .in_5(_8ram_16bit_7_p1), .in_6(_8ram_16bit_8_p1),
    .in_7(undriven), .out(OUT));
endmodule
