// Digital circuit 8RAM_16bit.dig as structural Verilog
module _8RAM_16bit (
  input  LOAD,
  input  [2:0] SEL,
  input  [15:0] IN,
  output [15:0] OUT
);

  wire demultiplexer_1_out_0, demultiplexer_1_out_1, demultiplexer_1_out_2, demultiplexer_1_out_3,
       demultiplexer_1_out_4, demultiplexer_1_out_5, demultiplexer_1_out_6, demultiplexer_1_out_7;
  wire [15:0] undriven, undriven_2, undriven_3, undriven_4, undriven_5, undriven_6, undriven_7, undriven_8;

  Demultiplexer #(.Selector_Bits(3)) demultiplexer_1 (
    .sel(SEL), .in(LOAD), .out_0(demultiplexer_1_out_0), .out_1(demultiplexer_1_out_1),
    .out_2(demultiplexer_1_out_2), .out_3(demultiplexer_1_out_3), .out_4(demultiplexer_1_out_4),
    .out_5(demultiplexer_1_out_5), .out_6(demultiplexer_1_out_6), .out_7(demultiplexer_1_out_7));
  Register_16bit register_16bit_1 (.IN(IN), .LOAD(demultiplexer_1_out_0));  // open: OUT
  Register_16bit register_16bit_2 (.IN(IN), .LOAD(demultiplexer_1_out_1));  // open: OUT
  Register_16bit register_16bit_3 (.IN(IN), .LOAD(demultiplexer_1_out_2));  // open: OUT
  Register_16bit register_16bit_4 (.IN(IN), .LOAD(demultiplexer_1_out_3));  // open: OUT
  Register_16bit register_16bit_5 (.IN(IN), .LOAD(demultiplexer_1_out_4));  // open: OUT
  Register_16bit register_16bit_6 (.IN(IN), .LOAD(demultiplexer_1_out_5));  // open: OUT
  Register_16bit register_16bit_7 (.IN(IN), .LOAD(demultiplexer_1_out_6));  // open: OUT
  Register_16bit register_16bit_8 (.IN(IN), .LOAD(demultiplexer_1_out_7));  // open: OUT
  Multiplexer #(.Selector_Bits(3), .Bits(16)) multiplexer_1 (
    .sel(SEL), .in_0(undriven_4), .in_1(undriven), .in_2(undriven_2), .in_3(undriven_3), .in_4(undriven_5),
    .in_5(undriven_6), .in_6(undriven_7), .in_7(undriven_8), .out(OUT));
endmodule
