// Digital circuit ALU_16bit.dig as structural Verilog
// zx | nx | zy | ny | f | no | out
//  1 | 0 | 1 | 0 | 1 | 0 | 0
//  1 | 1 | 1 | 1 | 1 | 1 | 1
//  1 | 1 | 1 | 0 | 1 | 0 | -1
//  0 | 0 | 1 | 1 | 0 | 0 | x
//  1 | 1 | 0 | 0 | 0 | 0 | y
//  0 | 0 | 1 | 1 | 0 | 1 | !x
//  1 | 1 | 0 | 0 | 0 | 1 | !y
//  0 | 0 | 1 | 1 | 1 | 1 | -x
//  1 | 1 | 0 | 0 | 1 | 1 | -y
//  0 | 1 | 1 | 1 | 1 | 1 | x+1
//  1 | 1 | 0 | 1 | 1 | 1 | y+1
//  0 | 0 | 1 | 1 | 1 | 0 | x-1
//  1 | 1 | 0 | 0 | 1 | 0 | y-1
//  0 | 0 | 0 | 0 | 1 | 0 | x+y
//  0 | 1 | 0 | 0 | 1 | 1 | x-y
//  0 | 0 | 0 | 1 | 1 | 1 | y-x
//  0 | 0 | 0 | 0 | 0 | 0 | x&y
//  0 | 1 | 0 | 1 | 0 | 1 | x|y
module ALU_16bit (
  input  [15:0] X,
  input  [15:0] Y,
  input  ZX,
  input  ZY,
  input  NX,
  input  NY,
  input  F,
  input  NO,
  output [15:0] OUT,
  output ZR,
  output NG
);

  wire or_1_out, or_2_out, or_3_out, or_4_out;
  wire [15:0] and_1_out, multiplexer_1_out, multiplexer_2_out, multiplexer_3_out, multiplexer_4_out,
       multiplexer_5_out, not_1_out, not_2_out, not_3_out, undriven;

  Multiplexer #(.Bits(16)) multiplexer_1 (.sel(ZX), .in_0(X), .in_1({16{1'b0}}), .out(multiplexer_1_out));
  Multiplexer #(.Bits(16)) multiplexer_2 (.sel(ZY), .in_0(Y), .in_1({16{1'b0}}), .out(multiplexer_2_out));
  assign not_1_out = ~multiplexer_1_out;  // Not not_1, 16 bits wide
  assign not_2_out = ~multiplexer_2_out;  // Not not_2, 16 bits wide
  Multiplexer #(.Bits(16)) multiplexer_3 (
    .sel(NX), .in_0(multiplexer_1_out), .in_1(not_1_out), .out(multiplexer_3_out));
  Multiplexer #(.Bits(16)) multiplexer_4 (
    .sel(NY), .in_0(multiplexer_2_out), .in_1(not_2_out), .out(multiplexer_4_out));
  assign and_1_out = multiplexer_3_out & multiplexer_4_out;  // And and_1, 16 bits wide
  // Additition_16bit additition_16bit_1: pin names not known; wires that end beside it: multiplexer_3_out, multiplexer_4_out, 1'b0
  Multiplexer #(.Bits(16)) multiplexer_5 (.sel(F), .in_0(and_1_out), .in_1(undriven), .out(multiplexer_5_out));
  assign not_3_out = ~multiplexer_5_out;  // Not not_3, 16 bits wide
  Multiplexer #(.Bits(16)) multiplexer_6 (.sel(NO), .in_0(multiplexer_5_out), .in_1(not_3_out), .out({NG, OUT[14:0]}));
  or or_1 (or_1_out, OUT[0], OUT[1], OUT[2], OUT[3], OUT[4]);
  or or_2 (or_2_out, OUT[5], OUT[6], OUT[7], OUT[8], OUT[9]);
  or or_3 (or_3_out, OUT[10], OUT[11], OUT[12], OUT[13], OUT[14]);
  or or_4 (or_4_out, or_3_out, NG);
  nor nor_1 (ZR, or_1_out, or_2_out, or_4_out);

  assign OUT[15] = NG;
endmodule
