// Digital circuit Additition_16bit.dig as structural Verilog
module Additition_16bit (
  input  CIN,
  input  [15:0] A,
  input  [15:0] B,
  output [15:0] SUM,
  output COUT
);

  wire full_adder_1bit_1_p5, full_adder_1bit_2_p5, full_adder_1bit_3_p5, full_adder_1bit_4_p5,
       full_adder_1bit_5_p5, full_adder_1bit_6_p5, full_adder_1bit_7_p5, full_adder_1bit_8_p5,
       full_adder_1bit_9_p5, full_adder_1bit_10_p5, full_adder_1bit_11_p5, full_adder_1bit_12_p5,
       full_adder_1bit_13_p5, full_adder_1bit_14_p5, full_adder_1bit_15_p5;

  // Full_adder_1bit full_adder_1bit_1: pin names not known; wires that end beside it: CIN, A[0], B[0], SUM[0], full_adder_1bit_1_p5
  // Full_adder_1bit full_adder_1bit_2: pin names not known; wires that end beside it: full_adder_1bit_1_p5, A[1], B[1], SUM[1], full_adder_1bit_2_p5
  // Full_adder_1bit full_adder_1bit_3: pin names not known; wires that end beside it: full_adder_1bit_2_p5, A[2], B[2], SUM[2], full_adder_1bit_3_p5
  // Full_adder_1bit full_adder_1bit_4: pin names not known; wires that end beside it: full_adder_1bit_3_p5, A[3], B[3], SUM[3], full_adder_1bit_4_p5
  // Full_adder_1bit full_adder_1bit_5: pin names not known; wires that end beside it: full_adder_1bit_4_p5, A[4], B[4], SUM[4], full_adder_1bit_5_p5
  // Full_adder_1bit full_adder_1bit_6: pin names not known; wires that end beside it: full_adder_1bit_5_p5, A[5], B[5], SUM[5], full_adder_1bit_6_p5
  // Full_adder_1bit full_adder_1bit_7: pin names not known; wires that end beside it: full_adder_1bit_6_p5, A[6], B[6], SUM[6], full_adder_1bit_7_p5
  // Full_adder_1bit full_adder_1bit_8: pin names not known; wires that end beside it: full_adder_1bit_7_p5, A[7], B[7], SUM[7], full_adder_1bit_8_p5
  // Full_adder_1bit full_adder_1bit_9: pin names not known; wires that end beside it: full_adder_1bit_8_p5, A[8], B[8], SUM[8], full_adder_1bit_9_p5
  // Full_adder_1bit full_adder_1bit_10: pin names not known; wires that end beside it: full_adder_1bit_9_p5, A[9], B[9], SUM[9], full_adder_1bit_10_p5
  // Full_adder_1bit full_adder_1bit_11: pin names not known; wires that end beside it: full_adder_1bit_10_p5, A[10], B[10], SUM[10], full_adder_1bit_11_p5
  // Full_adder_1bit full_adder_1bit_12: pin names not known; wires that end beside it: full_adder_1bit_11_p5, A[11], B[11], SUM[11], full_adder_1bit_12_p5
  // Full_adder_1bit full_adder_1bit_13: pin names not known; wires that end beside it: full_adder_1bit_12_p5, A[12], B[12], SUM[12], full_adder_1bit_13_p5
  // Full_adder_1bit full_adder_1bit_14: pin names not known; wires that end beside it: full_adder_1bit_13_p5, A[13], B[13], SUM[13], full_adder_1bit_14_p5
  // Full_adder_1bit full_adder_1bit_15: pin names not known; wires that end beside it: full_adder_1bit_14_p5, A[14], B[14], SUM[14], full_adder_1bit_15_p5
  // Full_adder_1bit full_adder_1bit_16: pin names not known; wires that end beside it: full_adder_1bit_15_p5, A[15], B[15], SUM[15], COUT
endmodule
