// Digital circuit CPU_without_control.dig as structural Verilog
module CPU_without_control (
  input  [15:0] inM,
  input  [15:0] Ins,
  input  [15:0] Reset,
  input  loadA,
  input  loadD,
  input  AorC,
  input  AorM,
  input  ZX,
  input  ZY,
  input  NX,
  input  NY,
  input  F,
  input  NO,
  output [15:0] PC,
  output NG,
  output ZR,
  output [15:0] addressM,
  output [15:0] outM
);

  wire alu_16bit_1_p1;
  wire [15:0] multiplexer_1_out, multiplexer_2_out;

  Multiplexer #(.Bits(16)) multiplexer_1 (.sel(AorC), .in_0(Ins), .in_1(outM), .out(multiplexer_1_out));
  Register_16bit A_Register (.IN(multiplexer_1_out), .LOAD(loadA));  // open: OUT
  Register_16bit D_Register (.IN(outM), .LOAD(loadD));  // open: OUT
  Multiplexer #(.Bits(16)) multiplexer_2 (.sel(AorM), .in_0(addressM), .in_1(inM), .out(multiplexer_2_out));
  // ALU_16bit alu_16bit_1: pin names not known; wires that end beside it: alu_16bit_1_p1, alu_16bit_1_p1, multiplexer_2_out, ZX, ZY, NX, NY, F, NO
  Program_counter_16bit program_counter_16bit_1 ();  // open: IN, INC, LOAD, RESET, EN, OUT
endmodule
