// Digital circuit Full_adder_1bit.dig as structural Verilog
module Full_adder_1bit (
  input  B,
  input  C,
  input  A,
  output SUM,
  output CARRY
);

  wire half_adder_1bit_1_p3, half_adder_1bit_1_p4, half_adder_1bit_2_p4;

  // Half_adder_1bit half_adder_1bit_1: pin names not known; wires that end beside it: C, A, half_adder_1bit_1_p3, half_adder_1bit_1_p4
  // Half_adder_1bit half_adder_1bit_2: pin names not known; wires that end beside it: half_adder_1bit_1_p3, B, SUM, half_adder_1bit_2_p4
  or or_1 (CARRY, half_adder_1bit_1_p4, half_adder_1bit_2_p4);
endmodule
