// Digital circuit Half_adder_1bit.dig as structural Verilog
module Half_adder_1bit (
  input  A,
  input  B,
  output SUM,
  output CARRY
);

  xor xor_1 (SUM, A, B);
  and and_1 (CARRY, A, B);
endmodule
