// Digital circuit Program_counter_16bit.dig as structural Verilog
module Program_counter_16bit (
  input  [15:0] IN,
  input  INC,
  input  LOAD,
  input  RESET,
  input  EN,
  output [15:0] OUT
);

  wire not_1_out, not_2_out;
  wire [15:0] multiplexer_1_out, multiplexer_2_out, multiplexer_3_out, undriven, undriven_2;

  // Additition_16bit additition_16bit_1: pin names not known; wires that end beside it: OUT, 16'h1, 1'b0
  Multiplexer #(.Bits(16)) multiplexer_1 (.sel(INC), .in_0(OUT), .in_1(undriven), .out(multiplexer_1_out));
  Multiplexer #(.Bits(16)) multiplexer_2 (.sel(LOAD), .in_0(multiplexer_1_out), .in_1(IN), .out(multiplexer_2_out));
  Multiplexer #(.Bits(16)) multiplexer_3 (
    .sel(RESET), .in_0(multiplexer_2_out), .in_1({16{1'b0}}), .out(multiplexer_3_out));
  Register_16bit register_16bit_1 (.IN(undriven_2), .LOAD(not_1_out));  // open: OUT
  not not_1 (not_1_out, not_2_out);
  Register_16bit register_16bit_2 (.IN(multiplexer_3_out), .LOAD(not_2_out));  // open: OUT
  not not_2 (not_2_out, EN);
endmodule
