// Digital circuit Register_16bit.dig as structural Verilog
module Register_16bit (
  input  [15:0] IN,
  input  LOAD,
  output [15:0] OUT
);

  Memory_1bit memory_1bit_1 (.D(IN[0]), .EN(LOAD));  // open: OUT
  Memory_1bit memory_1bit_2 (.D(IN[1]), .EN(LOAD));  // open: OUT
  Memory_1bit memory_1bit_3 (.D(IN[2]), .EN(LOAD));  // open: OUT
  Memory_1bit memory_1bit_4 (.D(IN[3]), .EN(LOAD));  // open: OUT
  Memory_1bit memory_1bit_5 (.D(IN[4]), .EN(LOAD));  // open: OUT
  Memory_1bit memory_1bit_6 (.D(IN[5]), .EN(LOAD));  // open: OUT
  Memory_1bit memory_1bit_7 (.D(IN[6]), .EN(LOAD));  // open: OUT
  Memory_1bit memory_1bit_8 (.D(IN[7]), .EN(LOAD));  // open: OUT
  Memory_1bit memory_1bit_9 (.D(IN[8]), .EN(LOAD));  // open: OUT
  Memory_1bit memory_1bit_10 (.D(IN[9]), .EN(LOAD));  // open: OUT
  Memory_1bit memory_1bit_11 (.D(IN[10]), .EN(LOAD));  // open: OUT
  Memory_1bit memory_1bit_12 (.D(IN[11]), .EN(LOAD));  // open: OUT
  Memory_1bit memory_1bit_13 (.D(IN[12]), .EN(LOAD));  // open: OUT
  Memory_1bit memory_1bit_14 (.D(IN[13]), .EN(LOAD));  // open: OUT
  Memory_1bit memory_1bit_15 (.D(IN[14]), .EN(LOAD));  // open: OUT
  Memory_1bit memory_1bit_16 (.D(IN[15]), .EN(LOAD));  // open: OUT
endmodule
